# Fritzing sketch ESP32_IoT_Thermostat (saved by Fritzing 0.8.7b)
breadboards: 3

parts:
  U1 = ESP32-38PinWide [part_number=ESP32-38PinWide]
  Part1 = BME280
  OLED_I2C1 = OLED 128x64 I2C Monochrome Display
  LED1 = LED - 3mm [color="Red (633nm)" package="3 mm [THT]"]
  R1 = Resistor [tolerance=±1% resistance=330 package=THT]
  S1 = Pushbutton [package="[THT]"]
  S2 = Pushbutton [package="[THT]"]
  R2 = Resistor [tolerance=±1% resistance=10k package=THT]
  R3 = Resistor [tolerance=±1% resistance=10k package=THT]
  C1 = Ceramic Capacitor [capacitance=100nF package="200 mil [THT, multilayer]"]
  C2 = Ceramic Capacitor [capacitance=100nF package="200 mil [THT, multilayer]"]

nets:
  VIN: U1.3.3, Part1.VIN, OLED_I2C1.VDD, S1.Pin_3, S1.Pin_4, S2.Pin_3, S2.Pin_4
  N1: U1.GPIO26, LED1.anode
  GND: U1.GND, Part1.GND, OLED_I2C1.GND, R1.Pin_1, R2.Pin_1, R3.Pin_1, C1.0, C2.0
  N2: U1.GPIO2, S1.Pin_1, S1.Pin_2, R3.Pin_0, C1.1
  N3: U1.GPIO5, S2.Pin_1, S2.Pin_2, R2.Pin_0, C2.1
  N4: U1.GPIO21, Part1.SDA, OLED_I2C1.SDA
  N5: U1.GPIO22, Part1.SCL, OLED_I2C1.SCK
  N6: LED1.cathode, R1.Pin_0

custom parts:
  ESP32-38PinWide: Generic 38-Pin ESP32 with wide format (only access to one side of pins on a breadboard) based on Stephen Lilley's HiLetgo ESP-WROOM-32 ESP32 ESP-32S Development Board.
