# Fritzing sketch Thermostat_Local (saved by Fritzing 0.8.7b)
breadboards: 2

parts:
  U1 = ESP32-38PinWide [part_number=ESP32-38PinWide]
  Part1 = BME280
  OLED_I2C1 = OLED 128x64 I2C Monochrome Display

nets:
  VIN: U1.3.3, Part1.VIN, OLED_I2C1.VDD
  GND: U1.GND, Part1.GND, OLED_I2C1.GND
  N1: U1.GPIO21, Part1.SDA, OLED_I2C1.SDA
  N2: U1.GPIO22, Part1.SCL, OLED_I2C1.SCK

custom parts:
  ESP32-38PinWide: Generic 38-Pin ESP32 with wide format (only access to one side of pins on a breadboard) based on Stephen Lilley's HiLetgo ESP-WROOM-32 ESP32 ESP-32S Development Board.
